// Logisim project lab41.circ as structural Verilog: 1 circuit, main circuit main
module main (
  input  x1,
  input  x2,
  input  p,
  output res,
  output \tran 
);

  wire and_1_out, and_2_out, and_3_out, and_4_out, and_5_out, and_6_out, and_7_out, not_1_out, not_2_out,
       not_3_out;

  not not_1 (not_1_out, x1);
  not not_2 (not_2_out, x2);
  not not_3 (not_3_out, p);
  and and_1 (and_1_out, not_1_out, p);
  and and_2 (and_2_out, not_1_out, x2);
  and and_3 (and_3_out, x2, p);
  and and_4 (and_4_out, not_1_out, not_2_out, p);
  and and_5 (and_5_out, not_1_out, x2, not_3_out);
  and and_6 (and_6_out, x1, not_2_out, not_3_out);
  and and_7 (and_7_out, x1, x2, p);
  or or_1 (res, and_1_out, and_2_out, and_3_out);
  or or_2 (\tran , and_4_out, and_5_out, and_6_out, and_7_out);

  // Notes on the sheet:
  //   x1
  //   x2
  //   p
  //   !x2
  //   !x1
  //   !p
  //   ODV3
endmodule
