// Logisim project lab42.circ as structural Verilog: 1 circuit, main circuit main
module main (
  input  x1,
  input  x2,
  input  x3,
  input  x4,
  output y1,
  output y2,
  output y3,
  output y4
);

  wire and_1_out, and_2_out, not_1_out, not_2_out, not_4_out;

  not not_1 (not_1_out, x1);
  not not_2 (not_2_out, x2);
  not not_3 (y3, x3);
  not not_4 (not_4_out, x4);
  and and_1 (and_1_out, x3, not_4_out);
  and and_2 (and_2_out, y3, x4);
  or or_1 (y4, and_1_out, and_2_out);

  assign y1 = x1;
  assign y2 = x2;

  // Notes on the sheet:
  //   x3
  //   x1
  //   x2
  //   !x1
  //   x4
  //   !x2
  //   !x3
  //   !x4
  //   D8425
endmodule
