// Logisim project вычитатель.circ as structural Verilog: 1 circuit, main circuit main
module main (
  input  _1
);

  wire and_1_out, and_2_out, clock_1_out, t_ff_1_qn, t_ff_2_qn;
  wire [2:0] t_ff_1_q;

  Clock clock_1 (.out(clock_1_out));
  and and_1 (and_1_out, t_ff_1_qn, _1);
  and and_2 (and_2_out, and_1_out, t_ff_2_qn);
  // Probe on t_ff_1_q
  T_Flip_Flop #(.Pre_Clr_Positions("LEGACY"), .enable("true"), .NewFFLayout("false")) t_ff_1 (
    .clk(clock_1_out), .T(_1), .Q(t_ff_1_q[0]), .Qn(t_ff_1_qn));  // open: preset, reset, en
  T_Flip_Flop #(.Pre_Clr_Positions("LEGACY"), .enable("true"), .NewFFLayout("false")) t_ff_2 (
    .clk(clock_1_out), .T(and_1_out), .Q(t_ff_1_q[1]), .Qn(t_ff_2_qn));  // open: preset, reset, en
  T_Flip_Flop #(.Pre_Clr_Positions("LEGACY"), .enable("true"), .NewFFLayout("false")) t_ff_3 (
    .clk(clock_1_out), .T(and_2_out), .Q(t_ff_1_q[2]));  // open: Qn, preset, reset, en
endmodule
